# Fritzing sketch Temperature-Sensor-Connections (saved by Fritzing 0.9.3b)
breadboards: 1

parts:
  Raspberry_Pi_1 = Raspberry Pi 3 [part_number=RPI-3-V1.2]
  Q2 = Basic FET N-Channel [package="TO220 [THT]"]
  Q3 = Basic FET P-Channel [package="TO220 [THT]"]

nets:
  N1: Raspberry_Pi_1.GPIO2, Q2.drain
  N2: Raspberry_Pi_1.GPIO3, Q3.drain
  N3: Raspberry_Pi_1.GND, Q2.source, Q3.gate
